# Fritzing sketch pcb (saved by Fritzing 0.9.2b)
circuit board: 22cm x 24.5cm
breadboards: 1

parts:
  R1 = Resistor [tolerance=±0.05% resistance=1k package=THT]
  R2 = Resistor [tolerance=±0.05% resistance=1k package=THT]
  C2 = Ceramic Capacitor [capacitance=0.1µF package="200 mil [THT, multilayer]"]
  R3 = Resistor [tolerance=±0.05% resistance=1k package=THT]
  R4 = Resistor [tolerance=±0.05% resistance=1k package=THT]
  R5 = Resistor [tolerance=±0.05% resistance=1k package=THT]
  R6 = Resistor [tolerance=±0.05% resistance=1k package=THT]
  R7 = Resistor [tolerance=±0.05% resistance=1k package=THT]
  R8 = Resistor [tolerance=±0.05% resistance=1k package=THT]
  R9 = Resistor [tolerance=±0.05% resistance=1k package=THT]
  R10 = Resistor [tolerance=±0.05% resistance=1k package=THT]
  R11 = Resistor [tolerance=±0.05% resistance=1k package=THT]
  R12 = Resistor [tolerance=±0.05% resistance=1k package=THT]
  R13 = Resistor [tolerance=±0.05% resistance=1k package=THT]
  R14 = Resistor [tolerance=±0.05% resistance=1k package=THT]
  R15 = Resistor [tolerance=±0.05% resistance=1k package=THT]
  R16 = Resistor [tolerance=±0.05% resistance=1k package=THT]
  R17 = Resistor [tolerance=±0.05% resistance=1k package=THT]
  R18 = Resistor [tolerance=±0.05% resistance=1k package=THT]
  R19 = Resistor [tolerance=±0.05% resistance=1k package=THT]
  U4 = LED CUBE PINOUT [package=ledcube]
  C3 = Ceramic Capacitor [capacitance=0.1µF package="200 mil [THT, multilayer]"]
  CATHODES1_2 = LED cathodes [package="5 mm [THT]"]
  CATHODES1_3 = LED cathodes [package="5 mm [THT]"]
  CATHODES1_4 = LED cathodes [package="5 mm [THT]"]
  CATHODES1_5 = LED cathodes [package="5 mm [THT]"]
  CATHODES1_6 = LED cathodes [package="5 mm [THT]"]
  CATHODES1_7 = LED cathodes [package="5 mm [THT]"]
  CATHODES1_8 = LED cathodes [package="5 mm [THT]"]
  CATHODES2_1 = LED cathodes [package="5 mm [THT]"]
  CATHODES2_2 = LED cathodes [package="5 mm [THT]"]
  CATHODES2_6 = LED cathodes [package="5 mm [THT]"]
  CATHODES2_3 = LED cathodes [package="5 mm [THT]"]
  CATHODES2_7 = LED cathodes [package="5 mm [THT]"]
  CATHODES2_8 = LED cathodes [package="5 mm [THT]"]
  CATHODES2_4 = LED cathodes [package="5 mm [THT]"]
  CATHODES2_5 = LED cathodes [package="5 mm [THT]"]
  DM13A_-_GREEN_4 = DM13A [package=THT]
  C4 = Ceramic Capacitor [capacitance=0.1µF package="200 mil [THT, multilayer]"]
  DM13A_-_RED_4 = DM13A [package=THT]
  DM13A_-_BLUE_4 = DM13A [package=THT]
  C5 = Ceramic Capacitor [capacitance=0.1µF package="200 mil [THT, multilayer]"]
  R20 = Resistor [tolerance=±0.05% resistance=1k package=THT]
  SN54HCT541 = SN54HCT541
  R21 = Resistor [tolerance=±0.05% resistance=1k package=THT]
  R22 = Resistor [tolerance=±0.05% resistance=1k package=THT]
  CATHODES1_1 = LED cathodes [package="5 mm [THT]"]
  Q4 = BD136 [package="TO220 [THT]"]
  Q3 = BD136 [package="TO220 [THT]"]
  Q7 = BD136 [package="TO220 [THT]"]
  Q2 = BD136 [package="TO220 [THT]"]
  Q6 = BD136 [package="TO220 [THT]"]
  Q8 = BD136 [package="TO220 [THT]"]
  Q5 = BD136 [package="TO220 [THT]"]
  Q1 = BD136 [package="TO220 [THT]"]
  R26 = Resistor [tolerance=±0.05% resistance=1k package=THT]
  R27 = Resistor [tolerance=±0.05% resistance=1k package=THT]
  R28 = Resistor [tolerance=±0.05% resistance=1k package=THT]
  DM13A_-_BLUE_3 = DM13A [package=THT]
  DM13A_-_RED_3 = DM13A [package=THT]
  DM13A_-_GREEN_3 = DM13A [package=THT]
  C9 = Ceramic Capacitor [capacitance=0.1µF package="200 mil [THT, multilayer]"]
  C10 = Ceramic Capacitor [capacitance=0.1µF package="200 mil [THT, multilayer]"]
  C11 = Ceramic Capacitor [capacitance=0.1µF package="200 mil [THT, multilayer]"]
  CATHODES2_17 = LED cathodes [package="5 mm [THT]"]
  CATHODES2_18 = LED cathodes [package="5 mm [THT]"]
  CATHODES2_19 = LED cathodes [package="5 mm [THT]"]
  CATHODES2_20 = LED cathodes [package="5 mm [THT]"]
  CATHODES2_21 = LED cathodes [package="5 mm [THT]"]
  CATHODES2_22 = LED cathodes [package="5 mm [THT]"]
  CATHODES2_23 = LED cathodes [package="5 mm [THT]"]
  CATHODES2_24 = LED cathodes [package="5 mm [THT]"]
  CATHODES1_17 = LED cathodes [package="5 mm [THT]"]
  CATHODES1_18 = LED cathodes [package="5 mm [THT]"]
  CATHODES1_19 = LED cathodes [package="5 mm [THT]"]
  CATHODES1_20 = LED cathodes [package="5 mm [THT]"]
  CATHODES1_21 = LED cathodes [package="5 mm [THT]"]
  CATHODES1_22 = LED cathodes [package="5 mm [THT]"]
  CATHODES1_23 = LED cathodes [package="5 mm [THT]"]
  CATHODES1_24 = LED cathodes [package="5 mm [THT]"]
  R35 = Resistor [tolerance=±0.05% resistance=1k package=THT]
  R37 = Resistor [tolerance=±0.05% resistance=1k package=THT]
  R39 = Resistor [tolerance=±0.05% resistance=1k package=THT]
  DM13A_-_BLUE_2 = DM13A [package=THT]
  DM13A_-_RED_2 = DM13A [package=THT]
  DM13A_-_GREEN_2 = DM13A [package=THT]
  C15 = Ceramic Capacitor [capacitance=0.1µF package="200 mil [THT, multilayer]"]
  C16 = Ceramic Capacitor [capacitance=0.1µF package="200 mil [THT, multilayer]"]
  C17 = Ceramic Capacitor [capacitance=0.1µF package="200 mil [THT, multilayer]"]
  CATHODES2_33 = LED cathodes [package="5 mm [THT]"]
  CATHODES2_34 = LED cathodes [package="5 mm [THT]"]
  CATHODES2_35 = LED cathodes [package="5 mm [THT]"]
  CATHODES2_36 = LED cathodes [package="5 mm [THT]"]
  CATHODES2_37 = LED cathodes [package="5 mm [THT]"]
  CATHODES2_38 = LED cathodes [package="5 mm [THT]"]
  CATHODES2_39 = LED cathodes [package="5 mm [THT]"]
  CATHODES2_40 = LED cathodes [package="5 mm [THT]"]
  CATHODES1_33 = LED cathodes [package="5 mm [THT]"]
  CATHODES1_34 = LED cathodes [package="5 mm [THT]"]
  CATHODES1_35 = LED cathodes [package="5 mm [THT]"]
  CATHODES1_36 = LED cathodes [package="5 mm [THT]"]
  CATHODES1_37 = LED cathodes [package="5 mm [THT]"]
  CATHODES1_3_2 = LED cathodes [package="5 mm [THT]"]
  CATHODES1_39 = LED cathodes [package="5 mm [THT]"]
  CATHODES1_40 = LED cathodes [package="5 mm [THT]"]
  DM13A_-_BLUE_1 = DM13A [package=THT]
  DM13A_-_RED_1 = DM13A [package=THT]
  DM13A_-_GREEN_1 = DM13A [package=THT]
  C21 = Ceramic Capacitor [capacitance=0.1µF package="200 mil [THT, multilayer]"]
  C22 = Ceramic Capacitor [capacitance=0.1µF package="200 mil [THT, multilayer]"]
  C23 = Ceramic Capacitor [capacitance=0.1µF package="200 mil [THT, multilayer]"]
  CATHODES2_49 = LED cathodes [package="5 mm [THT]"]
  CATHODES2_50 = LED cathodes [package="5 mm [THT]"]
  CATHODES2_51 = LED cathodes [package="5 mm [THT]"]
  CATHODES2_52 = LED cathodes [package="5 mm [THT]"]
  CATHODES2_53 = LED cathodes [package="5 mm [THT]"]
  CATHODES2_54 = LED cathodes [package="5 mm [THT]"]
  CATHODES2_55 = LED cathodes [package="5 mm [THT]"]
  CATHODES2_56 = LED cathodes [package="5 mm [THT]"]
  CATHODES1_49 = LED cathodes [package="5 mm [THT]"]
  CATHODES1_50 = LED cathodes [package="5 mm [THT]"]
  CATHODES1_51 = LED cathodes [package="5 mm [THT]"]
  CATHODES1_52 = LED cathodes [package="5 mm [THT]"]
  CATHODES1_53 = LED cathodes [package="5 mm [THT]"]
  CATHODES1_54 = LED cathodes [package="5 mm [THT]"]
  CATHODES1_55 = LED cathodes [package="5 mm [THT]"]
  CATHODES1_56 = LED cathodes [package="5 mm [THT]"]
  POWER = Power Jack [package=power_jack_pth]
  R40 = Resistor [tolerance=±0.05% resistance=1k package=THT]
  R41 = Resistor [tolerance=±0.05% resistance=1k package=THT]
  3_3v = LED - 5mm [color="Red (633nm)" package="5 mm [THT]"]
  5v = LED - 5mm [color="Red (633nm)" package="5 mm [THT]"]
  C26 = Electrolytic Capacitor [capacitance=100µF package="100 mil [THT, electrolytic]"]
  C27 = Electrolytic Capacitor [capacitance=1000µF package="200 mil [THT, electrolytic]"]
  IC1 = LD1117
  4A = Pico fuse
  0_5A = Resistor [tolerance=±0.05% resistance=1k package=THT]
  S3 = Momentary Switch [package=tactile-pth]
  R42 = Resistor [tolerance=±0.05% resistance=1k package=THT]
  2DIL7 = Shunt / Jumper [form="♀ (female)"]
  2DIL8 = Shunt / Jumper [form="♀ (female)"]
  2DIL9 = Shunt / Jumper [form="♀ (female)"]
  2DIL10 = Shunt / Jumper [form="♀ (female)"]
  2DIL11 = Shunt / Jumper [form="♀ (female)"]
  2DIL12 = Shunt / Jumper [form="♀ (female)"]

nets:
  GND: R1.Pin_0, C2.0, R3.Pin_0, R4.Pin_0, R5.Pin_0, R7.Pin_0, R14.Pin_0, R15.Pin_0, R16.Pin_0, R17.Pin_0, R18.Pin_0, R19.Pin_0, U4.GND, C3.0, DM13A_-_GREEN_4.GND, C4.0, DM13A_-_RED_4.GND, DM13A_-_BLUE_4.GND, C5.0, R20.Pin_1, SN54HCT541.GND, SN54HCT541.OE1, SN54HCT541.OE2, R21.Pin_1, R22.Pin_1, R26.Pin_1, R27.Pin_1, R28.Pin_1, DM13A_-_BLUE_3.GND, DM13A_-_RED_3.GND, DM13A_-_GREEN_3.GND, C9.0, C10.0, C11.0, R35.Pin_1, R37.Pin_1, R39.Pin_1, DM13A_-_BLUE_2.GND, DM13A_-_RED_2.GND, DM13A_-_GREEN_2.GND, C15.0, C16.0, C17.0, DM13A_-_BLUE_1.GND, DM13A_-_RED_1.GND, DM13A_-_GREEN_1.GND, C21.0, C22.0, C23.0, POWER.GNDBREAK, C26.-, C27.+, IC1.GND, S3.4, 2DIL7.2, 2DIL8.1
  N1: R1.Pin_1, Q1.collector
  N2: R2.Pin_0, Q1.base
  N3: R2.Pin_1, SN54HCT541.1Y
  VDD: C2.1, U4.5V, C3.1, DM13A_-_GREEN_4.VDD, C4.1, DM13A_-_RED_4.VDD, DM13A_-_BLUE_4.VDD, C5.1, SN54HCT541.VCC, Q4.emitter, Q3.emitter, Q7.emitter, Q2.emitter, Q6.emitter, Q8.emitter, Q5.emitter, Q1.emitter, DM13A_-_BLUE_3.VDD, DM13A_-_RED_3.VDD, DM13A_-_GREEN_3.VDD, C9.1, C10.1, C11.1, DM13A_-_BLUE_2.VDD, DM13A_-_RED_2.VDD, DM13A_-_GREEN_2.VDD, C15.1, C16.1, C17.1, DM13A_-_BLUE_1.VDD, DM13A_-_RED_1.VDD, DM13A_-_GREEN_1.VDD, C21.1, C22.1, C23.1, 4A.Pin_0
  N4: R3.Pin_1, DM13A_-_RED_4.REXT
  N5: R4.Pin_1, DM13A_-_GREEN_4.REXT
  N6: R5.Pin_1, DM13A_-_BLUE_4.REXT
  N7: R6.Pin_0, SN54HCT541.2Y
  N8: R6.Pin_1, Q2.base
  N9: R7.Pin_1, Q2.collector
  N10: R8.Pin_0, SN54HCT541.3Y
  N11: R8.Pin_1, Q3.base
  N12: R9.Pin_0, SN54HCT541.4Y
  N13: R9.Pin_1, Q4.base
  N14: R10.Pin_0, SN54HCT541.5Y
  N15: R10.Pin_1, Q5.base
  N16: R11.Pin_0, SN54HCT541.6Y
  N17: R11.Pin_1, Q6.base
  N18: R12.Pin_0, SN54HCT541.7Y
  N19: R12.Pin_1, Q7.base
  N20: R13.Pin_0, SN54HCT541.8Y
  N21: R13.Pin_1, Q8.base
  N22: R14.Pin_1, Q3.collector
  N23: R15.Pin_1, Q4.collector
  N24: R16.Pin_1, Q5.collector
  N25: R17.Pin_1, Q6.collector
  N26: R18.Pin_1, Q7.collector
  N27: R19.Pin_1, Q8.collector
  N28: U4.LAYER_8, SN54HCT541.8A
  N29: U4.CLOCK, DM13A_-_GREEN_4.DCK, DM13A_-_RED_4.DCK, DM13A_-_BLUE_4.DCK, DM13A_-_BLUE_3.DCK, DM13A_-_RED_3.DCK, DM13A_-_GREEN_3.DCK, DM13A_-_BLUE_2.DCK, DM13A_-_RED_2.DCK, DM13A_-_GREEN_2.DCK, DM13A_-_BLUE_1.DCK, DM13A_-_RED_1.DCK, DM13A_-_GREEN_1.DCK, 2DIL9.2
  N30: U4.LAYER_7, SN54HCT541.7A
  N31: U4.LAYER_6, SN54HCT541.6A
  N32: U4.ENABLE, CATHODES1_3.red_cathode, CATHODES1_3.green_cathode, CATHODES1_3.blue_cathode, DM13A_-_GREEN_4.EN, DM13A_-_GREEN_4.OUT10, DM13A_-_RED_4.EN, DM13A_-_RED_4.OUT10, DM13A_-_BLUE_4.EN, DM13A_-_BLUE_4.OUT10, DM13A_-_BLUE_3.EN, DM13A_-_BLUE_3.OUT10, DM13A_-_RED_3.EN, DM13A_-_RED_3.OUT10, DM13A_-_GREEN_3.EN, DM13A_-_GREEN_3.OUT10, CATHODES1_22.red_cathode, CATHODES1_22.green_cathode, CATHODES1_22.blue_cathode, DM13A_-_BLUE_2.EN, DM13A_-_BLUE_2.OUT10, DM13A_-_RED_2.EN, DM13A_-_RED_2.OUT10, DM13A_-_GREEN_2.EN, DM13A_-_GREEN_2.OUT10, CATHODES1_3_2.red_cathode, CATHODES1_3_2.green_cathode, CATHODES1_3_2.blue_cathode, DM13A_-_BLUE_1.EN, DM13A_-_BLUE_1.OUT10, DM13A_-_RED_1.EN, DM13A_-_RED_1.OUT10, DM13A_-_GREEN_1.EN, DM13A_-_GREEN_1.OUT10, CATHODES1_54.red_cathode, CATHODES1_54.green_cathode, CATHODES1_54.blue_cathode, 2DIL8.2
  N33: U4.LAYER_5, SN54HCT541.5A
  N34: U4.LATCH, DM13A_-_GREEN_4.LAT, DM13A_-_RED_4.LAT, DM13A_-_BLUE_4.LAT, DM13A_-_BLUE_3.LAT, DM13A_-_RED_3.LAT, DM13A_-_GREEN_3.LAT, DM13A_-_BLUE_2.LAT, DM13A_-_RED_2.LAT, DM13A_-_GREEN_2.LAT, DM13A_-_BLUE_1.LAT, DM13A_-_RED_1.LAT, DM13A_-_GREEN_1.LAT, 2DIL9.1
  N35: U4.LAYER_4, SN54HCT541.4A
  N36: U4.RESET, R42.Pin_0
  N37: U4.LAYER_3, SN54HCT541.3A
  N38: U4.RED, DM13A_-_RED_1.DAI, 2DIL11.1
  N39: U4.LAYER_2, SN54HCT541.2A
  N40: U4.LAYER_1, SN54HCT541.1A
  N41: U4.GREEN, DM13A_-_GREEN_1.DAI, 2DIL12.1
  N42: U4.3.3V, 3_3v.anode, 0_5A.Pin_1
  N43: U4.BLUE, DM13A_-_BLUE_1.DAI, 2DIL10.1
  N44: CATHODES1_2.red_cathode, DM13A_-_RED_4.OUT9
  N45: CATHODES1_2.green_cathode, DM13A_-_GREEN_4.OUT9
  N46: CATHODES1_2.blue_cathode, DM13A_-_BLUE_4.OUT9
  N47: CATHODES1_4.red_cathode, DM13A_-_RED_4.OUT11
  N48: CATHODES1_4.green_cathode, DM13A_-_GREEN_4.OUT11
  N49: CATHODES1_4.blue_cathode, DM13A_-_BLUE_4.OUT11
  N50: CATHODES1_5.red_cathode, DM13A_-_RED_4.OUT12
  N51: CATHODES1_5.green_cathode, DM13A_-_GREEN_4.OUT12
  N52: CATHODES1_5.blue_cathode, DM13A_-_BLUE_4.OUT12
  N53: CATHODES1_6.red_cathode, DM13A_-_RED_4.OUT13
  N54: CATHODES1_6.green_cathode, DM13A_-_GREEN_4.OUT13
  N55: CATHODES1_6.blue_cathode, DM13A_-_BLUE_4.OUT13
  N56: CATHODES1_7.red_cathode, DM13A_-_RED_4.OUT14
  N57: CATHODES1_7.green_cathode, DM13A_-_GREEN_4.OUT14
  N58: CATHODES1_7.blue_cathode, DM13A_-_BLUE_4.OUT14
  N59: CATHODES1_8.red_cathode, DM13A_-_RED_4.OUT15
  N60: CATHODES1_8.green_cathode, DM13A_-_GREEN_4.OUT15
  N61: CATHODES1_8.blue_cathode, DM13A_-_BLUE_4.OUT15
  N62: CATHODES2_1.red_cathode, DM13A_-_RED_4.OUT0
  N63: CATHODES2_1.green_cathode, DM13A_-_GREEN_4.OUT0
  N64: CATHODES2_1.blue_cathode, DM13A_-_BLUE_4.OUT0
  N65: CATHODES2_2.red_cathode, DM13A_-_RED_4.OUT1
  N66: CATHODES2_2.green_cathode, DM13A_-_GREEN_4.OUT1
  N67: CATHODES2_2.blue_cathode, DM13A_-_BLUE_4.OUT1
  N68: CATHODES2_6.red_cathode, DM13A_-_RED_4.OUT5
  N69: CATHODES2_6.green_cathode, DM13A_-_GREEN_4.OUT5
  N70: CATHODES2_6.blue_cathode, DM13A_-_BLUE_4.OUT5
  N71: CATHODES2_3.red_cathode, DM13A_-_RED_4.OUT2
  N72: CATHODES2_3.green_cathode, DM13A_-_GREEN_4.OUT2
  N73: CATHODES2_3.blue_cathode, DM13A_-_BLUE_4.OUT2
  N74: CATHODES2_7.red_cathode, DM13A_-_RED_4.OUT6
  N75: CATHODES2_7.green_cathode, DM13A_-_GREEN_4.OUT6
  N76: CATHODES2_7.blue_cathode, DM13A_-_BLUE_4.OUT6
  N77: CATHODES2_8.red_cathode, DM13A_-_RED_4.OUT7
  N78: CATHODES2_8.green_cathode, DM13A_-_GREEN_4.OUT7
  N79: CATHODES2_8.blue_cathode, DM13A_-_BLUE_4.OUT7
  N80: CATHODES2_4.red_cathode, DM13A_-_RED_4.OUT3
  N81: CATHODES2_4.green_cathode, DM13A_-_GREEN_4.OUT3
  N82: CATHODES2_4.blue_cathode, DM13A_-_BLUE_4.OUT3
  N83: CATHODES2_5.red_cathode, DM13A_-_RED_4.OUT4
  N84: CATHODES2_5.green_cathode, DM13A_-_GREEN_4.OUT4
  N85: CATHODES2_5.blue_cathode, DM13A_-_BLUE_4.OUT4
  N86: DM13A_-_GREEN_4.DAI, DM13A_-_GREEN_3.DAO
  N87: DM13A_-_GREEN_4.DAO, 2DIL11.2
  N88: DM13A_-_GREEN_4.OUT8, CATHODES1_1.green_cathode
  N89: DM13A_-_RED_4.DAI, DM13A_-_RED_3.DAO
  N90: DM13A_-_RED_4.DAO, 2DIL10.2
  N91: DM13A_-_RED_4.OUT8, CATHODES1_1.red_cathode
  N92: DM13A_-_BLUE_4.DAI, DM13A_-_BLUE_3.DAO
  N93: DM13A_-_BLUE_4.DAO, 2DIL12.2
  N94: DM13A_-_BLUE_4.OUT8, CATHODES1_1.blue_cathode
  N95: R20.Pin_0, DM13A_-_RED_3.REXT
  N96: R21.Pin_0, DM13A_-_GREEN_3.REXT
  N97: R22.Pin_0, DM13A_-_BLUE_3.REXT
  N98: R26.Pin_0, DM13A_-_BLUE_2.REXT
  N99: R27.Pin_0, DM13A_-_GREEN_2.REXT
  N100: R28.Pin_0, DM13A_-_RED_2.REXT
  N101: DM13A_-_BLUE_3.DAI, DM13A_-_BLUE_2.DAO
  N102: DM13A_-_BLUE_3.OUT0, CATHODES2_24.blue_cathode
  N103: DM13A_-_BLUE_3.OUT1, CATHODES2_23.blue_cathode
  N104: DM13A_-_BLUE_3.OUT2, CATHODES2_21.blue_cathode
  N105: DM13A_-_BLUE_3.OUT3, CATHODES2_18.blue_cathode
  N106: DM13A_-_BLUE_3.OUT4, CATHODES2_17.blue_cathode
  N107: DM13A_-_BLUE_3.OUT5, CATHODES2_22.blue_cathode
  N108: DM13A_-_BLUE_3.OUT6, CATHODES2_20.blue_cathode
  N109: DM13A_-_BLUE_3.OUT7, CATHODES2_19.blue_cathode
  N110: DM13A_-_BLUE_3.OUT8, CATHODES1_24.blue_cathode
  N111: DM13A_-_BLUE_3.OUT9, CATHODES1_23.blue_cathode
  N112: DM13A_-_BLUE_3.OUT11, CATHODES1_21.blue_cathode
  N113: DM13A_-_BLUE_3.OUT12, CATHODES1_20.blue_cathode
  N114: DM13A_-_BLUE_3.OUT13, CATHODES1_19.blue_cathode
  N115: DM13A_-_BLUE_3.OUT14, CATHODES1_18.blue_cathode
  N116: DM13A_-_BLUE_3.OUT15, CATHODES1_17.blue_cathode
  N117: DM13A_-_RED_3.DAI, DM13A_-_RED_2.DAO
  N118: DM13A_-_RED_3.OUT0, CATHODES2_24.red_cathode
  N119: DM13A_-_RED_3.OUT1, CATHODES2_23.red_cathode
  N120: DM13A_-_RED_3.OUT2, CATHODES2_21.red_cathode
  N121: DM13A_-_RED_3.OUT3, CATHODES2_18.red_cathode
  N122: DM13A_-_RED_3.OUT4, CATHODES2_17.red_cathode
  N123: DM13A_-_RED_3.OUT5, CATHODES2_22.red_cathode
  N124: DM13A_-_RED_3.OUT6, CATHODES2_20.red_cathode
  N125: DM13A_-_RED_3.OUT7, CATHODES2_19.red_cathode
  N126: DM13A_-_RED_3.OUT8, CATHODES1_24.red_cathode
  N127: DM13A_-_RED_3.OUT9, CATHODES1_23.red_cathode
  N128: DM13A_-_RED_3.OUT11, CATHODES1_21.red_cathode
  N129: DM13A_-_RED_3.OUT12, CATHODES1_20.red_cathode
  N130: DM13A_-_RED_3.OUT13, CATHODES1_19.red_cathode
  N131: DM13A_-_RED_3.OUT14, CATHODES1_18.red_cathode
  N132: DM13A_-_RED_3.OUT15, CATHODES1_17.red_cathode
  N133: DM13A_-_GREEN_3.DAI, DM13A_-_GREEN_2.DAO
  N134: DM13A_-_GREEN_3.OUT0, CATHODES2_24.green_cathode
  N135: DM13A_-_GREEN_3.OUT1, CATHODES2_23.green_cathode
  N136: DM13A_-_GREEN_3.OUT2, CATHODES2_21.green_cathode
  N137: DM13A_-_GREEN_3.OUT3, CATHODES2_18.green_cathode
  N138: DM13A_-_GREEN_3.OUT4, CATHODES2_17.green_cathode
  N139: DM13A_-_GREEN_3.OUT5, CATHODES2_22.green_cathode
  N140: DM13A_-_GREEN_3.OUT6, CATHODES2_20.green_cathode
  N141: DM13A_-_GREEN_3.OUT7, CATHODES2_19.green_cathode
  N142: DM13A_-_GREEN_3.OUT8, CATHODES1_24.green_cathode
  N143: DM13A_-_GREEN_3.OUT9, CATHODES1_23.green_cathode
  N144: DM13A_-_GREEN_3.OUT11, CATHODES1_21.green_cathode
  N145: DM13A_-_GREEN_3.OUT12, CATHODES1_20.green_cathode
  N146: DM13A_-_GREEN_3.OUT13, CATHODES1_19.green_cathode
  N147: DM13A_-_GREEN_3.OUT14, CATHODES1_18.green_cathode
  N148: DM13A_-_GREEN_3.OUT15, CATHODES1_17.green_cathode
  N149: R35.Pin_0, DM13A_-_BLUE_1.REXT
  N150: R37.Pin_0, DM13A_-_GREEN_1.REXT
  N151: R39.Pin_0, DM13A_-_RED_1.REXT
  N152: DM13A_-_BLUE_2.DAI, DM13A_-_BLUE_1.DAO
  N153: DM13A_-_BLUE_2.OUT0, CATHODES2_40.blue_cathode
  N154: DM13A_-_BLUE_2.OUT1, CATHODES2_39.blue_cathode
  N155: DM13A_-_BLUE_2.OUT2, CATHODES2_37.blue_cathode
  N156: DM13A_-_BLUE_2.OUT3, CATHODES2_34.blue_cathode
  N157: DM13A_-_BLUE_2.OUT4, CATHODES2_33.blue_cathode
  N158: DM13A_-_BLUE_2.OUT5, CATHODES2_38.blue_cathode
  N159: DM13A_-_BLUE_2.OUT6, CATHODES2_36.blue_cathode
  N160: DM13A_-_BLUE_2.OUT7, CATHODES2_35.blue_cathode
  N161: DM13A_-_BLUE_2.OUT8, CATHODES1_40.blue_cathode
  N162: DM13A_-_BLUE_2.OUT9, CATHODES1_39.blue_cathode
  N163: DM13A_-_BLUE_2.OUT11, CATHODES1_37.blue_cathode
  N164: DM13A_-_BLUE_2.OUT12, CATHODES1_36.blue_cathode
  N165: DM13A_-_BLUE_2.OUT13, CATHODES1_35.blue_cathode
  N166: DM13A_-_BLUE_2.OUT14, CATHODES1_34.blue_cathode
  N167: DM13A_-_BLUE_2.OUT15, CATHODES1_33.blue_cathode
  N168: DM13A_-_RED_2.DAI, DM13A_-_RED_1.DAO
  N169: DM13A_-_RED_2.OUT0, CATHODES2_40.red_cathode
  N170: DM13A_-_RED_2.OUT1, CATHODES2_39.red_cathode
  N171: DM13A_-_RED_2.OUT2, CATHODES2_37.red_cathode
  N172: DM13A_-_RED_2.OUT3, CATHODES2_34.red_cathode
  N173: DM13A_-_RED_2.OUT4, CATHODES2_33.red_cathode
  N174: DM13A_-_RED_2.OUT5, CATHODES2_38.red_cathode
  N175: DM13A_-_RED_2.OUT6, CATHODES2_36.red_cathode
  N176: DM13A_-_RED_2.OUT7, CATHODES2_35.red_cathode
  N177: DM13A_-_RED_2.OUT8, CATHODES1_40.red_cathode
  N178: DM13A_-_RED_2.OUT9, CATHODES1_39.red_cathode
  N179: DM13A_-_RED_2.OUT11, CATHODES1_37.red_cathode
  N180: DM13A_-_RED_2.OUT12, CATHODES1_36.red_cathode
  N181: DM13A_-_RED_2.OUT13, CATHODES1_35.red_cathode
  N182: DM13A_-_RED_2.OUT14, CATHODES1_34.red_cathode
  N183: DM13A_-_RED_2.OUT15, CATHODES1_33.red_cathode
  N184: DM13A_-_GREEN_2.DAI, DM13A_-_GREEN_1.DAO
  N185: DM13A_-_GREEN_2.OUT0, CATHODES2_40.green_cathode
  N186: DM13A_-_GREEN_2.OUT1, CATHODES2_39.green_cathode
  N187: DM13A_-_GREEN_2.OUT2, CATHODES2_37.green_cathode
  N188: DM13A_-_GREEN_2.OUT3, CATHODES2_34.green_cathode
  N189: DM13A_-_GREEN_2.OUT4, CATHODES2_33.green_cathode
  N190: DM13A_-_GREEN_2.OUT5, CATHODES2_38.green_cathode
  N191: DM13A_-_GREEN_2.OUT6, CATHODES2_36.green_cathode
  N192: DM13A_-_GREEN_2.OUT7, CATHODES2_35.green_cathode
  N193: DM13A_-_GREEN_2.OUT8, CATHODES1_40.green_cathode
  N194: DM13A_-_GREEN_2.OUT9, CATHODES1_39.green_cathode
  N195: DM13A_-_GREEN_2.OUT11, CATHODES1_37.green_cathode
  N196: DM13A_-_GREEN_2.OUT12, CATHODES1_36.green_cathode
  N197: DM13A_-_GREEN_2.OUT13, CATHODES1_35.green_cathode
  N198: DM13A_-_GREEN_2.OUT14, CATHODES1_34.green_cathode
  N199: DM13A_-_GREEN_2.OUT15, CATHODES1_33.green_cathode
  N200: DM13A_-_BLUE_1.OUT0, CATHODES2_56.blue_cathode
  N201: DM13A_-_BLUE_1.OUT1, CATHODES2_55.blue_cathode
  N202: DM13A_-_BLUE_1.OUT2, CATHODES2_53.blue_cathode
  N203: DM13A_-_BLUE_1.OUT3, CATHODES2_50.blue_cathode
  N204: DM13A_-_BLUE_1.OUT4, CATHODES2_49.blue_cathode
  N205: DM13A_-_BLUE_1.OUT5, CATHODES2_54.blue_cathode
  N206: DM13A_-_BLUE_1.OUT6, CATHODES2_52.blue_cathode
  N207: DM13A_-_BLUE_1.OUT7, CATHODES2_51.blue_cathode
  N208: DM13A_-_BLUE_1.OUT8, CATHODES1_56.blue_cathode
  N209: DM13A_-_BLUE_1.OUT9, CATHODES1_55.blue_cathode
  N210: DM13A_-_BLUE_1.OUT11, CATHODES1_53.blue_cathode
  N211: DM13A_-_BLUE_1.OUT12, CATHODES1_52.blue_cathode
  N212: DM13A_-_BLUE_1.OUT13, CATHODES1_51.blue_cathode
  N213: DM13A_-_BLUE_1.OUT14, CATHODES1_50.blue_cathode
  N214: DM13A_-_BLUE_1.OUT15, CATHODES1_49.blue_cathode
  N215: DM13A_-_RED_1.OUT0, CATHODES2_56.red_cathode
  N216: DM13A_-_RED_1.OUT1, CATHODES2_55.red_cathode
  N217: DM13A_-_RED_1.OUT2, CATHODES2_53.red_cathode
  N218: DM13A_-_RED_1.OUT3, CATHODES2_50.red_cathode
  N219: DM13A_-_RED_1.OUT4, CATHODES2_49.red_cathode
  N220: DM13A_-_RED_1.OUT5, CATHODES2_54.red_cathode
  N221: DM13A_-_RED_1.OUT6, CATHODES2_52.red_cathode
  N222: DM13A_-_RED_1.OUT7, CATHODES2_51.red_cathode
  N223: DM13A_-_RED_1.OUT8, CATHODES1_56.red_cathode
  N224: DM13A_-_RED_1.OUT9, CATHODES1_55.red_cathode
  N225: DM13A_-_RED_1.OUT11, CATHODES1_53.red_cathode
  N226: DM13A_-_RED_1.OUT12, CATHODES1_52.red_cathode
  N227: DM13A_-_RED_1.OUT13, CATHODES1_51.red_cathode
  N228: DM13A_-_RED_1.OUT14, CATHODES1_50.red_cathode
  N229: DM13A_-_RED_1.OUT15, CATHODES1_49.red_cathode
  N230: DM13A_-_GREEN_1.OUT0, CATHODES2_56.green_cathode
  N231: DM13A_-_GREEN_1.OUT1, CATHODES2_55.green_cathode
  N232: DM13A_-_GREEN_1.OUT2, CATHODES2_53.green_cathode
  N233: DM13A_-_GREEN_1.OUT3, CATHODES2_50.green_cathode
  N234: DM13A_-_GREEN_1.OUT4, CATHODES2_49.green_cathode
  N235: DM13A_-_GREEN_1.OUT5, CATHODES2_54.green_cathode
  N236: DM13A_-_GREEN_1.OUT6, CATHODES2_52.green_cathode
  N237: DM13A_-_GREEN_1.OUT7, CATHODES2_51.green_cathode
  N238: DM13A_-_GREEN_1.OUT8, CATHODES1_56.green_cathode
  N239: DM13A_-_GREEN_1.OUT9, CATHODES1_55.green_cathode
  N240: DM13A_-_GREEN_1.OUT11, CATHODES1_53.green_cathode
  N241: DM13A_-_GREEN_1.OUT12, CATHODES1_52.green_cathode
  N242: DM13A_-_GREEN_1.OUT13, CATHODES1_51.green_cathode
  N243: DM13A_-_GREEN_1.OUT14, CATHODES1_50.green_cathode
  N244: DM13A_-_GREEN_1.OUT15, CATHODES1_49.green_cathode
  N245: POWER.PWR, 5v.anode, C26.+, C27.-, IC1.IN, 4A.Pin_1
  N246: R40.Pin_0, 5v.cathode
  N247: R40.Pin_1, R41.Pin_1, 2DIL7.1
  N248: R41.Pin_0, 3_3v.cathode
  N249: IC1.OUT, 0_5A.Pin_0
  N250: S3.1, S3.2, R42.Pin_1

custom parts:
  LED cathodes: Pin out for connecting LED RGB cathodes
  DM13A: 16-bit Constant Current LED Driver
  SN54HCT541: OCTAL BUFFERS AND LINE DRIVERS WITH 3-STATE OUTPUTS
  BD136: A pnp transistor which can drive a higher load
  LD1117: Low drop fixed and adjustable positive voltage regulators
  Pico fuse: Pico Fuse (4A)
  Shunt / Jumper: 2 pin DIL shunt
